// Logisim project alpha.circ as structural Verilog
module instruction_type (
  input  [6:0] opcode,
  output [3:0] inst_t
);

  PLA #(.in_width(7), .out_width(4), .\table ("xxxxxx0 0000 # X (compressed)\nxxxxx01 0000 # X (compressed)\n0000011 0101 # LOAD\n0000111 0000 # X (LOAD-FP)\n0001011 0000 # X (custom-0)\n0001111 0000 # X (MISC-MEM)\n0010011 0010 # OP-IMM\n0010111 0011 # AUIPC\n0011011 0000 # X (OP-IMM-32)\n0011111 0000 # X (48b inst)\n0100011 0110 # STORE\n0100111 0000 # X (STORE-FP)\n0101011 0000 # X (custom-1)\n0101111 0000 # X (AMO)\n0110011 0001 # OP\n0110111 0100 # LUI\n0111011 0000 # X (OP-32)\n0111111 0000 # X (64b inst)\n1000011 0000 # X (MADD)\n1000111 0000 # X (MSUB)\n1001011 0000 # X (NMSUB)\n1001111 0000 # X (NMADD)\n1010011 0000 # X (OP-FP)\n1010111 0000 # X (reserved)\n1011011 0000 # X (custom-2)\n1011111 0000 # X (48b inst)\n1100011 0111 # BRANCH\n1100111 1000 # JALR\n1101011 0000 # X (reserved)\n1101111 1001 # JAL\n1110011 1010 # SYSTEM\n1110111 0000 # X (reserved)\n1111011 0000 # X (custom-3)\n1111111 0000 # X (80b+ inst)")) pla_1 (
    .in(opcode), .out(inst_t));

  // Notes on the sheet:
  //   Instruction type decode
  //   Decode the instruction type from the opcode. Values for inst_t are documented in the alpha.md file.
endmodule

module instruction_decode (
  input  [31:0] instruction,
  output [6:0] opcode,
  output [4:0] rd,
  output [2:0] funct3,
  output [4:0] rs1,
  output [4:0] rs2,
  output [6:0] funct7,
  output [31:0] imm_i,
  output [31:0] imm_s,
  output [31:0] imm_b,
  output [31:0] imm_u,
  output [31:0] imm_j
);

  assign imm_i = {{20{instruction[31]}}, instruction[31:20]};  // Bit_Extender bit_extender_1
  assign imm_s = {{20{instruction[31]}}, {instruction[31:25], instruction[11:7]}};  // Bit_Extender bit_extender_2
  assign imm_b = {{19{instruction[31]}}, {instruction[31], instruction[7], instruction[30:25], instruction[11:8], 1'b0}};  // Bit_Extender bit_extender_3
  assign imm_j = {{11{instruction[31]}}, {instruction[31], instruction[19:12], instruction[20], instruction[30:21], 1'b0}};  // Bit_Extender bit_extender_4

  assign funct3 = instruction[14:12];
  assign funct7 = instruction[31:25];
  assign imm_u = {instruction[31:12], {12{1'b0}}};
  assign opcode = instruction[6:0];
  assign rd = instruction[11:7];
  assign rs1 = instruction[19:15];
  assign rs2 = instruction[24:20];

  // Notes on the sheet:
  //   Instruction decode
  //   Decode a 32-bit instruction into its parts. This circuit provides parts for all instruction types.
endmodule

module state_machine (
  input  [3:0] inst_t,
  input  illegal,
  input  clk,
  input  rst,
  output [1:0] rd_select,
  output [1:0] pc_select,
  output [1:0] mem_select,
  output mem_w,
  output mem_rd,
  output load_inst,
  output [1:0] state
);

  wire [1:0] pla_6_out;
  wire [3:0] multiplexer_1_out;
  wire [4:4] pla_1_out;

  Multiplexer #(.width(4)) multiplexer_1 (.in0(inst_t), .in1(4'b0000), .out(multiplexer_1_out), .sel(illegal));
  PLA #(.out_width(1), .\table ("00 1 # continue\n01 0 # single\n10 1 # double\n11 0 # halt")) pla_1 (
    .in(state), .out(pla_1_out[4]));
  PLA #(.in_width(5), .\table ("00000 00 # X\n00001 10 # OP\n00010 10 # OP_IMM\n00011 10 # AUIPC\n00100 10 # LUI\n00101 11 # LOAD\n00110 00 # STORE\n00111 00 # BRANCH\n01000 01 # JALR\n01001 01 # JAL\n01010 00 # SYSTEM\n01011 00 # X\n011xx 00 # X\n1xxxx 00 # continue")) pla_2 (
    .in({pla_1_out[4], multiplexer_1_out}), .out(rd_select));
  PLA #(.in_width(5), .\table ("00000 00 # X\n00001 01 # OP\n00010 01 # OP_IMM\n00011 01 # AUIPC\n00100 01 # LUI\n00101 01 # LOAD\n00110 01 # STORE\n00111 10 # BRANCH\n01000 10 # JALR\n01001 10 # JAL\n01010 00 # SYSTEM\n01011 00 # X\n011xx 00 # X\n1xxxx 00 # continue")) pla_3 (
    .in({pla_1_out[4], multiplexer_1_out}), .out(pc_select));
  PLA #(.in_width(5), .out_width(4), .\table ("00000 0000 # X\n00001 0001 # OP\n00010 0001 # OP_IMM\n00011 0001 # AUIPC\n00100 0001 # LUI\n00101 1010 # LOAD\n00110 0110 # STORE\n00111 0000 # BRANCH\n01000 0000 # JALR\n01001 0000 # JAL\n01010 0000 # SYSTEM\n01011 0000 # X\n011xx 0000 # X\n1xxxx 0000 # continue")) pla_4 (
    .in({pla_1_out[4], multiplexer_1_out}), .out({mem_rd, mem_w, mem_select}));
  PLA #(.in_width(5), .out_width(1), .\table ("00000 0 # X\n00001 1 # OP\n00010 1 # OP_IMM\n00011 1 # AUIPC\n00100 1 # LUI\n00101 0 # LOAD\n00110 0 # STORE\n00111 0 # BRANCH\n01000 0 # JALR\n01001 0 # JAL\n01010 0 # SYSTEM\n01011 0 # X\n011xx 0 # X\n1xxxx 1 # continue")) pla_5 (
    .in({pla_1_out[4], multiplexer_1_out}), .out(load_inst));
  PLA #(.in_width(5), .\table ("00000 11 # X\n00001 01 # OP\n00010 01 # OP_IMM\n00011 01 # AUIPC\n00100 01 # LUI\n00101 10 # LOAD\n00110 10 # STORE\n00111 00 # BRANCH\n01000 00 # JALR\n01001 00 # JAL\n01010 11 # SYSTEM\n01011 11 # X\n011xx 11 # X\n1xxxx 01 # continue")) pla_6 (
    .in({pla_1_out[4], multiplexer_1_out}), .out(pla_6_out));
  Register #(.width(2)) register_1 (.D(pla_6_out), .en(1'b1), .clk(clk), .Q(state), .clr(rst));

  // Notes on the sheet:
  //   State machine
  //   States are described in the alpha.md file.
  //   0 => none, 1 => pc_next, 2 => rd_val, 3 => mem
  //   0 => pc, 1 => pc_next, 2 => rd_val
  //   0 => pc, 1 => pc_next, 2 => rd_val
endmodule

module subword_processing (
  input  mem_w_in,
  input  mem_rd_in,
  input  [31:0] mem_addr,
  input  [31:0] mem_out,
  input  [31:0] rs2_val,
  input  [2:0] funct3,
  input  illegal_in,
  output [31:0] rd_in,
  output [31:0] mem_in,
  output mem_w_out,
  output illegal_out
);

  wire subword_load_processing_1_illegal_out, subword_store_processing_1_illegal_out;

  subword_load_processing subword_load_processing_1 (
    .mem_addr(mem_addr), .mem_out(mem_out), .mem_rd_in(mem_rd_in), .funct3(funct3), .illegal_in(illegal_in),
    .illegal_out(subword_load_processing_1_illegal_out), .rd_in(rd_in));
  subword_store_processing subword_store_processing_1 (
    .mem_addr(mem_addr), .mem_out(mem_out), .rs2_val(rs2_val), .funct3(funct3), .mem_w_in(mem_w_in),
    .illegal_in(illegal_in), .illegal_out(subword_store_processing_1_illegal_out), .mem_w_out(mem_w_out),
    .mem_in(mem_in));
  or or_1 (illegal_out, subword_load_processing_1_illegal_out, subword_store_processing_1_illegal_out);

  // Notes on the sheet:
  //   Subword processing
  //   Split into load processing and store processing.
endmodule

module subword_load_processing (
  input  [31:0] mem_addr,
  input  [31:0] mem_out,
  input  mem_rd_in,
  input  [2:0] funct3,
  input  illegal_in,
  output illegal_out,
  output [31:0] rd_in
);

  wire and_1_out, multiplexer_5_out, or_1_out;
  wire [7:0] multiplexer_2_out;
  wire [15:0] multiplexer_1_out;
  wire [31:0] bit_extender_1_out, bit_extender_2_out, bit_extender_3_out, bit_extender_4_out,
       multiplexer_3_out, multiplexer_4_out;

  Multiplexer #(.width(16)) multiplexer_1 (
    .in0(mem_out[15:0]), .in1(mem_out[31:16]), .out(multiplexer_1_out), .sel(mem_addr[1]));
  Multiplexer #(.select(2), .width(8)) multiplexer_2 (
    .in0(mem_out[7:0]), .in1(mem_out[15:8]), .in2(mem_out[23:16]), .in3(mem_out[31:24]),
    .out(multiplexer_2_out), .sel(mem_addr[1:0]));
  assign bit_extender_1_out = {{16{multiplexer_1_out[15]}}, multiplexer_1_out};  // Bit_Extender bit_extender_1
  assign bit_extender_2_out = {{16{1'b0}}, multiplexer_1_out};  // Bit_Extender bit_extender_2
  assign bit_extender_3_out = {{24{multiplexer_2_out[7]}}, multiplexer_2_out};  // Bit_Extender bit_extender_3
  assign bit_extender_4_out = {{24{1'b0}}, multiplexer_2_out};  // Bit_Extender bit_extender_4
  or or_1 (or_1_out, mem_addr[1], funct3[2], mem_addr[0]);
  Multiplexer #(.width(32)) multiplexer_3 (
    .in0(bit_extender_1_out), .in1(bit_extender_2_out), .out(multiplexer_3_out), .sel(funct3[2]));
  Multiplexer #(.width(32)) multiplexer_4 (
    .in0(bit_extender_3_out), .in1(bit_extender_4_out), .out(multiplexer_4_out), .sel(funct3[2]));
  Multiplexer #(.select(2)) multiplexer_5 (
    .in0(1'b0), .in1(mem_addr[0]), .in2(or_1_out), .in3(1'b1), .out(multiplexer_5_out), .sel(funct3[1:0]));
  and and_1 (and_1_out, multiplexer_5_out, illegal_in);
  and and_2 (illegal_out, and_1_out, mem_rd_in);
  Multiplexer #(.select(2), .width(32)) multiplexer_6 (
    .in0(multiplexer_4_out), .in1(multiplexer_3_out), .in2(mem_out), .in3(mem_out), .out(rd_in),
    .sel(funct3[1:0]));

  // Notes on the sheet:
  //   Subword load processing
  //   Extract and properly extend value from memory to store in register.
endmodule

module subword_store_processing (
  input  [31:0] mem_addr,
  input  [31:0] mem_out,
  input  [31:0] rs2_val,
  input  [2:0] funct3,
  input  mem_w_in,
  input  illegal_in,
  output illegal_out,
  output mem_w_out,
  output [31:0] mem_in
);

  wire and_1_out, multiplexer_11_out, multiplexer_13_out, or_1_out;
  wire [7:0] multiplexer_3_out, multiplexer_4_out, multiplexer_5_out, multiplexer_6_out, multiplexer_7_out,
       multiplexer_8_out, multiplexer_9_out, multiplexer_10_out;
  wire [15:0] multiplexer_1_out, multiplexer_2_out;

  or or_1 (or_1_out, mem_addr[0], mem_addr[1]);
  Multiplexer #(.width(16)) multiplexer_1 (
    .in0(rs2_val[15:0]), .in1(mem_out[15:0]), .out(multiplexer_1_out), .sel(mem_addr[1]));
  Multiplexer #(.width(16)) multiplexer_2 (
    .in0(mem_out[31:16]), .in1(rs2_val[15:0]), .out(multiplexer_2_out), .sel(mem_addr[1]));
  Multiplexer #(.width(8)) multiplexer_3 (
    .in0(rs2_val[7:0]), .in1(mem_out[7:0]), .out(multiplexer_3_out), .sel(mem_addr[0]));
  Multiplexer #(.width(8)) multiplexer_4 (
    .in0(multiplexer_3_out), .in1(mem_out[7:0]), .out(multiplexer_4_out), .sel(mem_addr[1]));
  Multiplexer #(.width(8)) multiplexer_5 (
    .in0(mem_out[15:8]), .in1(rs2_val[7:0]), .out(multiplexer_5_out), .sel(mem_addr[0]));
  Multiplexer #(.width(8)) multiplexer_6 (
    .in0(multiplexer_5_out), .in1(mem_out[15:8]), .out(multiplexer_6_out), .sel(mem_addr[1]));
  Multiplexer #(.width(8)) multiplexer_7 (
    .in0(mem_out[23:16]), .in1(multiplexer_8_out), .out(multiplexer_7_out), .sel(mem_addr[1]));
  Multiplexer #(.width(8)) multiplexer_8 (
    .in0(rs2_val[7:0]), .in1(mem_out[23:16]), .out(multiplexer_8_out), .sel(mem_addr[0]));
  Multiplexer #(.width(8)) multiplexer_9 (
    .in0(mem_out[31:24]), .in1(multiplexer_10_out), .out(multiplexer_9_out), .sel(mem_addr[1]));
  Multiplexer #(.width(8)) multiplexer_10 (
    .in0(mem_out[31:24]), .in1(rs2_val[7:0]), .out(multiplexer_10_out), .sel(mem_addr[0]));
  Multiplexer #(.select(2)) multiplexer_11 (
    .in0(1'b0), .in1(mem_addr[0]), .in2(or_1_out), .in3(1'b1), .out(multiplexer_11_out), .sel(funct3[1:0]));
  Multiplexer #(.select(2), .width(32)) multiplexer_12 (
    .in0({multiplexer_9_out, multiplexer_7_out, multiplexer_6_out, multiplexer_4_out}),
    .in1({multiplexer_2_out, multiplexer_1_out}), .in2(rs2_val),
    .in3({multiplexer_9_out, multiplexer_7_out, multiplexer_6_out, multiplexer_4_out}), .out(mem_in),
    .sel(funct3[1:0]));
  Multiplexer multiplexer_13 (.in0(multiplexer_11_out), .in1(1'b1), .out(multiplexer_13_out), .sel(funct3[2]));
  and and_1 (and_1_out, multiplexer_13_out, illegal_in);
  and and_2 (illegal_out, and_1_out, mem_w_in);
  and and_3 (mem_w_out, ~and_1_out, mem_w_in);  // AND_Gate

  // Notes on the sheet:
  //   Subword store processing
  //   Extract and properly extend value from register to store in memory.
endmodule
